# Fritzing sketch i2c_oled (saved by Fritzing 0.9.2b)
breadboards: 1

parts:
  U1 = SIP - 4 pins [chip_label=Module package="SIP (Single Inline) [THT]"]
  U2 = ESP8266 WiFi Module [part_number=ESP8266]
  R1 = Resistor [tolerance=±5% resistance=10k package=THT]
  R2 = Resistor [tolerance=±5% resistance=10k package=THT]
  M1 = USB to Serial Module, 5 pins [chip_label=Module package="SIP (Single Inline) [THT]"]
  S1 = SWITCH-MOMENTARY-2 [package=tactile_switch_smd-2]
  U3 = SWITCH_SPDT [package=kps-1290]

nets:
  3.3V: U1.VCC, U2.VCC, R1.Pin_0, R2.Pin_0
  GND: U1.GND, U2.GND, M1.GND, S1.1, U3.O
  N1: U1.SCL, U3.S
  N2: U1.SDA, U2.GPIO_2
  N3: U2.RXD, M1.TXD
  N4: U2.GPIO_0, U3.P
  N5: U2.GPIO_16, R2.Pin_1, S1.2
  N6: U2.CH_PD, R1.Pin_1
  N7: U2.TXD, M1.RXD

notes:
  Pgrm/Run
  Reset

custom parts:
  SIP - 4 pins: A SIP stand-in part for whatever you want. With 4 pins on a 300 mil single inline package (SIP) footprint.
  ESP8266 WiFi Module: Generic WiFi Module based on the ESP8266 with onboard PCB antenna and UART communications
  USB to Serial Module, 5 pins: USB to 5v/3.3v TTL, 5pin
